// Logisim project 24hClock.circ as structural Verilog: 3 circuits, main circuit main
module base60Increment (
  input  Enable,
  input  Clk,
  input  RESET,
  output Q0,
  output Q1,
  output Q2,
  output Q3,
  output [5:0] out_8,
  output Q4,
  output Q5,
  output Overflow
);

  wire and_1_out, and_2_out, d_ff_1_q, t_ff_1_qn, t_ff_2_qn, t_ff_3_qn, t_ff_4_qn, t_ff_5_qn;

  T_Flip_Flop t_ff_1 (.T(Enable), .clk(Clk), .Q(out_8[0]), .Qn(t_ff_1_qn), .reset(Overflow));  // open: preset
  T_Flip_Flop t_ff_2 (.T(Enable), .clk(t_ff_1_qn), .Q(out_8[1]), .Qn(t_ff_2_qn), .reset(Overflow));  // open: preset
  T_Flip_Flop t_ff_3 (.T(Enable), .clk(t_ff_2_qn), .Q(out_8[2]), .Qn(t_ff_3_qn), .reset(Overflow));  // open: preset
  T_Flip_Flop t_ff_4 (.T(Enable), .clk(t_ff_3_qn), .Q(out_8[3]), .Qn(t_ff_4_qn), .reset(Overflow));  // open: preset
  T_Flip_Flop t_ff_5 (.T(Enable), .clk(t_ff_4_qn), .Q(out_8[4]), .Qn(t_ff_5_qn), .reset(Overflow));  // open: preset
  T_Flip_Flop t_ff_6 (.T(Enable), .clk(t_ff_5_qn), .Q(out_8[5]), .reset(Overflow));  // open: Qn, preset
  or or_1 (Overflow, and_2_out, d_ff_1_q);
  D_Flip_Flop d_ff_1 (.D(1'b1), .clk(RESET), .Q(d_ff_1_q), .reset(and_1_out));  // open: Qn, preset
  and and_1 (and_1_out, Clk, d_ff_1_q);
  and and_2 (and_2_out, out_8[5], out_8[4], out_8[3], out_8[2]);

  assign Q0 = out_8[0];
  assign Q1 = out_8[1];
  assign Q2 = out_8[2];
  assign Q3 = out_8[3];
  assign Q4 = out_8[4];
  assign Q5 = out_8[5];

  // Notes on the sheet:
  //   RESET: pull=down
endmodule

module main (
  input  in_1,
  output [5:0] out_2,
  output [5:0] out_3,
  output [4:0] out_4
);

  wire base60increment_1_overflow, base60increment_2_overflow, clock_1_out;

  Clock clock_1 (.out(clock_1_out));
  base60Increment base60increment_1 (
    .Enable(1'b1), .Clk(clock_1_out), .RESET(in_1), .Q0(out_2[0]), .Q1(out_2[1]), .Q2(out_2[2]),
    .Q3(out_2[3]), .Q4(out_2[4]), .Q5(out_2[5]), .Overflow(base60increment_1_overflow));  // open: out_8
  base60Increment base60increment_2 (
    .Enable(1'b1), .Clk(base60increment_1_overflow), .RESET(in_1), .Q0(out_3[0]), .Q1(out_3[1]),
    .Q2(out_3[2]), .Q3(out_3[3]), .Q4(out_3[4]), .Q5(out_3[5]), .Overflow(base60increment_2_overflow));  // open: out_8
  base24Increment base24increment_1 (
    .Enable(1'b1), .Clk(base60increment_2_overflow), .RESET(in_1), .Q0(out_4[0]), .Q1(out_4[1]),
    .Q2(out_4[2]), .Q3(out_4[3]), .Q4(out_4[4]));  // open: out_8, Overflow
endmodule

module base24Increment (
  input  Enable,
  input  Clk,
  input  RESET,
  output Q0,
  output Q1,
  output Q2,
  output Q3,
  output [4:0] out_8,
  output Q4,
  output Overflow
);

  wire and_1_out, and_2_out, d_ff_1_q, t_ff_1_qn, t_ff_2_qn, t_ff_3_qn, t_ff_4_qn;

  T_Flip_Flop t_ff_1 (.T(Enable), .clk(Clk), .Q(out_8[0]), .Qn(t_ff_1_qn), .reset(Overflow));  // open: preset
  T_Flip_Flop t_ff_2 (.T(Enable), .clk(t_ff_1_qn), .Q(out_8[1]), .Qn(t_ff_2_qn), .reset(Overflow));  // open: preset
  T_Flip_Flop t_ff_3 (.T(Enable), .clk(t_ff_2_qn), .Q(out_8[2]), .Qn(t_ff_3_qn), .reset(Overflow));  // open: preset
  T_Flip_Flop t_ff_4 (.T(Enable), .clk(t_ff_3_qn), .Q(out_8[3]), .Qn(t_ff_4_qn), .reset(Overflow));  // open: preset
  T_Flip_Flop t_ff_5 (.T(Enable), .clk(t_ff_4_qn), .Q(out_8[4]), .reset(Overflow));  // open: Qn, preset
  or or_1 (Overflow, and_2_out, d_ff_1_q);
  D_Flip_Flop d_ff_1 (.D(1'b1), .clk(RESET), .Q(d_ff_1_q), .reset(and_1_out));  // open: Qn, preset
  and and_1 (and_1_out, Clk, d_ff_1_q);
  and and_2 (and_2_out, out_8[4], out_8[3]);

  assign Q0 = out_8[0];
  assign Q1 = out_8[1];
  assign Q2 = out_8[2];
  assign Q3 = out_8[3];
  assign Q4 = out_8[4];

  // Notes on the sheet:
  //   RESET: pull=down
endmodule
