// Logisim project encoderReader.circ as structural Verilog: 3 circuits, main circuit reader
module reader (
  input  A,
  input  B,
  output dir,
  output impulsion
);

  wire not_1_out;

  D_Flip_Flop d_ff_1 (.D(not_1_out), .clk(A), .Q(dir));  // open: Qn, preset, reset
  not not_1 (not_1_out, B);

  assign impulsion = B;
endmodule

module antiRebond (
  input  dataIn,
  output dataOut
);

  wire and_1_out, and_2_out, clock_1_out, d_ff_1_q, d_ff_2_q, d_ff_3_q, d_ff_4_q, nor_1_out;

  Clock clock_1 (.out(clock_1_out));
  D_Flip_Flop d_ff_1 (.D(dataIn), .clk(clock_1_out), .Q(d_ff_1_q));  // open: Qn, preset, reset
  D_Flip_Flop d_ff_2 (.D(d_ff_1_q), .clk(clock_1_out), .Q(d_ff_2_q));  // open: Qn, preset, reset
  D_Flip_Flop d_ff_3 (.D(d_ff_2_q), .clk(clock_1_out), .Q(d_ff_3_q));  // open: Qn, preset, reset
  D_Flip_Flop d_ff_4 (.D(d_ff_3_q), .clk(clock_1_out), .Q(d_ff_4_q));  // open: Qn, preset, reset
  nor nor_1 (nor_1_out, d_ff_1_q, d_ff_2_q, d_ff_3_q);
  and and_1 (and_1_out, d_ff_1_q, d_ff_2_q, d_ff_3_q);
  assign dataOut = and_1_out ? and_1_out : 1'bz;  // Controlled_Buffer controlled_buffer_1
  and and_2 (and_2_out, ~and_1_out, ~nor_1_out);  // AND_Gate
  assign dataOut = and_2_out ? d_ff_4_q : 1'bz;  // Controlled_Buffer controlled_buffer_2
  assign dataOut = nor_1_out ? ~nor_1_out : 1'bz;  // Controlled_Inverter controlled_inverter_1
endmodule

module main (
  input  A,
  input  B,
  output direction,
  output impulsion
);

  wire ar2_dataout, ar_dataout;

  antiRebond ar (.dataIn(A), .dataOut(ar_dataout));
  antiRebond ar2 (.dataIn(B), .dataOut(ar2_dataout));
  reader r (.A(ar_dataout), .B(ar2_dataout), .dir(direction), .impulsion(impulsion));
endmodule
