// Logisim project main_circuit.circ as structural Verilog: 32 circuits, main circuit main
module main (
  input  em,
  input  a,
  input  b,
  input  ep,
  input  Encoder_button,
  input  Menu,
  output vcc,
  output gnd,
  output led,
  output [7:0] S0,
  output [7:0] S1,
  output [7:0] S2,
  output [7:0] S3,
  output [7:0] S4,
  output [7:0] S5
);

  wire e_emoins, e_eplus, not_1_out, or_1_out, or_2_out;

  encodeur e (.a(a), .b(b), .Emoins(e_emoins), .Eplus(e_eplus));
  or or_1 (or_1_out, em, e_emoins);
  or or_2 (or_2_out, e_eplus, ep);
  not not_1 (not_1_out, Encoder_button);
  screen_managment sm (
    .Eplus(or_2_out), .Eminus(or_1_out), .Enter(not_1_out), .Menu(Menu), .Sonnerie(led), .S0(S0), .S1(S1),
    .S2(S2), .S3(S3), .S4(S4), .S5(S5));

  assign gnd = 1'b0;
  assign vcc = 1'b1;
endmodule

module base24Increment (
  input  RESET,
  input  Enable,
  input  Clk,
  output Overflow,
  output [4:0] S
);

  wire not_1_out;

  Counter #(.max('h17), .width(5)) counter_1 (
    .clr(RESET), .load(1'b0), .up(not_1_out), .count(Enable), .clk(Clk), .carry(Overflow), .Q(S));  // open: D
  not not_1 (not_1_out, 1'b0);

  // Notes on the sheet:
  //   RESET: pull=down
endmodule

module base60Increment (
  input  RESET,
  input  Enable,
  input  Clk,
  output Overflow,
  output [5:0] S
);

  wire not_1_out;

  Counter #(.max('h3b), .width(6)) counter_1 (
    .clr(RESET), .load(1'b0), .up(not_1_out), .count(Enable), .clk(Clk), .carry(Overflow), .Q(S));  // open: D
  not not_1 (not_1_out, 1'b0);

  // Notes on the sheet:
  //   RESET: pull=down
endmodule

module timer (
  input  Enable,
  input  R,
  output [6:0] cS,
  output [5:0] S,
  output [5:0] M,
  output [4:0] H
);

  wire b1_overflow, b_clkout, clock_1_out, clock_2_out, wdojvn_overflow;

  Clock clock_1 (.out(clock_1_out));
  base100Increment b (.Enable(1'b0), .Clk(clock_1_out), .Reset(1'b0), .S(cS), .Clkout(b_clkout));  // open: Overflow
  Clock #(.highDuration(128), .lowDuration(128)) clock_2 (.out(clock_2_out));
  base60Increment b1 (.RESET(R), .Enable(Enable), .Clk(clock_2_out), .Overflow(b1_overflow), .S(S));
  base60Increment wdojvn (.RESET(R), .Enable(b1_overflow), .Clk(clock_2_out), .Overflow(wdojvn_overflow), .S(M));
  base24Increment wdkmv (.RESET(R), .Enable(wdojvn_overflow), .Clk(clock_2_out), .S(H));  // open: Overflow
endmodule

module shifteur4 (
  input  [3:0] E,
  output [3:0] S
);


  assign S = {E[2:0], 1'b0};
endmodule

module shifteur7 (
  input  [6:0] E,
  output [6:0] S
);


  assign S = {E[5:0], 1'b0};
endmodule

module decodeur_7seg_mieux (
  input  P,
  input  [4:0] E,
  output [7:0] S
);

  wire and_1_out, and_2_out, and_3_out, and_4_out, and_5_out, and_6_out, and_7_out, and_8_out, and_9_out,
       and_10_out, and_11_out, and_12_out, and_13_out, and_14_out, and_15_out, and_16_out, and_17_out,
       and_18_out, and_19_out, and_20_out, and_21_out, and_22_out, and_23_out, and_24_out, and_25_out,
       and_26_out, and_27_out, and_28_out, and_29_out, and_30_out, and_31_out, and_32_out, and_33_out,
       and_34_out, and_35_out, and_36_out, and_37_out, and_38_out, and_39_out, and_40_out, and_41_out,
       and_42_out, and_43_out, and_44_out, and_45_out, and_46_out, and_47_out, and_48_out, and_49_out,
       and_50_out, and_51_out, and_52_out, and_53_out, and_54_out, and_55_out, and_56_out, and_57_out,
       and_58_out, and_59_out, and_60_out, not_1_out, not_2_out, not_3_out, not_4_out, not_5_out;

  not not_1 (not_1_out, E[4]);
  not not_2 (not_2_out, E[3]);
  not not_3 (not_3_out, E[2]);
  not not_4 (not_4_out, E[1]);
  not not_5 (not_5_out, E[0]);
  and and_1 (and_1_out, not_3_out, not_4_out, not_5_out);
  and and_2 (and_2_out, not_1_out, E[1], not_5_out);
  and and_3 (and_3_out, not_2_out, E[1], E[0]);
  and and_4 (and_4_out, not_2_out, E[2], E[0]);
  and and_5 (and_5_out, not_1_out, E[2], E[1]);
  and and_6 (and_6_out, not_1_out, E[3], not_5_out);
  and and_7 (and_7_out, E[3], not_3_out, not_4_out);
  and and_8 (and_8_out, E[4], E[3], not_3_out, E[0]);
  and and_9 (and_9_out, not_1_out, not_2_out, not_3_out);
  and and_10 (and_10_out, not_1_out, not_2_out, not_4_out, not_5_out);
  and and_11 (and_11_out, not_1_out, not_3_out, not_4_out);
  and and_12 (and_12_out, not_2_out, E[1], E[0]);
  and and_13 (and_13_out, E[3], not_3_out, not_5_out);
  and and_14 (and_14_out, not_1_out, E[3], not_4_out, E[0]);
  and and_15 (and_15_out, E[4], not_2_out, E[0]);
  and and_16 (and_16_out, E[4], E[3], not_3_out, E[1]);
  and and_17 (and_17_out, E[4], E[3], E[1], not_5_out);
  and and_18 (and_18_out, not_1_out, not_2_out, not_4_out);
  and and_19 (and_19_out, not_1_out, not_3_out, not_4_out);
  and and_20 (and_20_out, not_2_out, not_3_out, not_4_out);
  and and_21 (and_21_out, not_1_out, not_4_out, E[0]);
  and and_22 (and_22_out, not_2_out, E[0]);
  and and_23 (and_23_out, not_3_out, not_4_out, E[0]);
  and and_24 (and_24_out, not_2_out, E[2], E[1]);
  and and_25 (and_25_out, not_1_out, E[3], not_3_out);
  and and_26 (and_26_out, E[3], not_3_out, E[1], not_5_out);
  and and_27 (and_27_out, E[4], E[2], E[1], E[0]);
  and and_28 (and_28_out, not_2_out, not_3_out, not_4_out, not_5_out);
  and and_29 (and_29_out, not_1_out, not_2_out, E[1], not_5_out);
  and and_30 (and_30_out, not_3_out, E[1], E[0]);
  and and_31 (and_31_out, not_1_out, E[2], not_4_out, E[0]);
  and and_32 (and_32_out, not_1_out, E[3], not_4_out);
  and and_33 (and_33_out, E[3], not_4_out, E[0]);
  and and_34 (and_34_out, not_1_out, E[3], E[2], not_5_out);
  and and_35 (and_35_out, E[4], not_2_out, not_4_out, not_5_out);
  and and_36 (and_36_out, E[4], E[1], E[0]);
  and and_37 (and_37_out, E[4], E[3], not_3_out, E[1]);
  and and_38 (and_38_out, not_3_out, not_5_out);
  and and_39 (and_39_out, not_2_out, E[1], not_5_out);
  and and_40 (and_40_out, E[3], E[1], E[0]);
  and and_41 (and_41_out, not_1_out, E[3], E[2]);
  and and_42 (and_42_out, E[4], not_2_out);
  and and_43 (and_43_out, not_3_out, not_4_out, not_5_out);
  and and_44 (and_44_out, not_1_out, E[2], not_5_out);
  and and_45 (and_45_out, not_2_out, E[2], not_4_out);
  and and_46 (and_46_out, not_1_out, E[3], not_3_out);
  and and_47 (and_47_out, not_1_out, E[3], E[1]);
  and and_48 (and_48_out, E[3], E[1], not_5_out);
  and and_49 (and_49_out, E[4], not_3_out, not_4_out);
  and and_50 (and_50_out, E[4], not_3_out, not_5_out);
  and and_51 (and_51_out, E[4], not_2_out, E[2], E[0]);
  and and_52 (and_52_out, not_1_out, not_3_out, E[1]);
  and and_53 (and_53_out, not_1_out, not_2_out, E[2], not_4_out);
  and and_54 (and_54_out, not_2_out, E[2], E[1], not_5_out);
  and and_55 (and_55_out, not_1_out, E[3], not_3_out);
  and and_56 (and_56_out, E[3], not_3_out, E[0]);
  and and_57 (and_57_out, E[3], not_4_out, E[0]);
  and and_58 (and_58_out, not_1_out, E[3], E[1]);
  and and_59 (and_59_out, E[4], not_3_out, not_4_out);
  and and_60 (and_60_out, E[4], E[3], not_4_out);
  or or_1 (S[0], and_1_out, and_2_out, and_3_out, and_4_out, and_5_out, and_6_out, and_7_out, and_8_out);
  or or_2 (S[1], and_9_out, and_10_out, and_11_out, and_12_out, and_13_out, and_14_out, and_15_out, and_16_out, and_17_out);
  or or_3 (S[2], and_18_out, and_19_out, and_20_out, and_21_out, and_22_out, and_23_out, and_24_out, and_25_out, and_26_out, and_27_out);
  or or_4 (S[3], and_28_out, and_29_out, and_30_out, and_31_out, and_32_out, and_33_out, and_34_out, and_35_out, and_36_out, and_37_out);
  or or_5 (S[4], and_38_out, and_39_out, and_40_out, and_41_out, and_42_out);
  or or_6 (S[5], and_43_out, and_44_out, and_45_out, and_46_out, and_47_out, and_48_out, and_49_out, and_50_out, and_51_out);
  or or_7 (S[6], and_52_out, and_53_out, and_54_out, and_55_out, and_56_out, and_57_out, and_58_out, and_59_out, and_60_out);

  assign S[7] = P;

  // Notes on the sheet:
  //   Chiffres de 0a9 puis lettres de AaZ
  //   Enfin, -,=,smiley(pt1),smiley(pt2)
  //   Manque k,q,r,t,v,w,x,y
  //   Ajouter t et r et espace
endmodule

module double_dabble_1step (
  input  [3:0] A0,
  input  [3:0] A1,
  input  [6:0] E,
  output [3:0] A0out,
  output [3:0] A1out,
  output [6:0] Eout
);

  wire [0:0] adder_3_cout, adder_3_out;
  wire [2:0] adder_3_out_2;
  wire [3:0] adder_1_out, adder_5_out, and_1_out, and_2_out, c1_s, c2_s, s1_s, s2_s;

  Adder #(.width(4)) adder_1 (.a({3'b000, adder_3_cout[0]}), .b(A1), .out(adder_1_out), .cin(1'b0));  // open: cout
  comparator5 c1 (.E(A0), .S(c1_s));
  shifteur4 s1 (.E(adder_5_out), .S(s1_s));
  shifteur4 s2 (.E({adder_3_out[0], adder_3_out_2}), .S(s2_s));
  assign and_1_out = c1_s & 4'b0011;  // AND_Gate and_1, 4 bits wide
  comparator5 c2 (.E(adder_1_out), .S(c2_s));
  Adder #(.width(4)) adder_2 (.a(s2_s), .b({3'b000, E[6]}), .out(A0out), .cin(1'b0));  // open: cout
  shifteur7 s3 (.E(E), .S(Eout));
  Adder #(.width(4)) adder_3 (
    .a(A0), .b(and_1_out), .out({adder_3_out[0], adder_3_out_2}), .cin(1'b0), .cout(adder_3_cout[0]));
  assign and_2_out = 4'b0011 & c2_s;  // AND_Gate and_2, 4 bits wide
  Adder #(.width(4)) adder_4 (.a(s1_s), .b({3'b000, adder_3_out[0]}), .out(A1out), .cin(1'b0));  // open: cout
  Adder #(.width(4)) adder_5 (.a(and_2_out), .b(A1), .out(adder_5_out), .cin(1'b0));  // open: cout

  // Notes on the sheet:
  //   A0'
  //   A1'
  //   A0out
  //   A1out
endmodule

module comparator5 (
  input  [3:0] E,
  output [3:0] S
);

  wire and_1_out, and_2_out;

  and and_1 (and_1_out, E[0], E[2]);
  and and_2 (and_2_out, E[1], E[2]);
  or or_1 (S[3], and_1_out, and_2_out, E[3]);

  assign S[2:0] = {3{S[3]}};
endmodule

module double_dabble (
  input  [6:0] E,
  output [3:0] A0,
  output [3:0] A1
);

  wire [3:0] d1_a0out, d1_a1out, d2_a0out, d2_a1out, d3_a0out, d3_a1out, d4_a0out, d4_a1out, d5_a0out,
       d5_a1out, d6_a0out, d6_a1out;
  wire [6:0] d1_eout, d2_eout, d3_eout, d4_eout, d5_eout, d6_eout;

  double_dabble_1step d1 (.A0(4'b0000), .A1(4'b0000), .E(E), .A0out(d1_a0out), .A1out(d1_a1out), .Eout(d1_eout));
  double_dabble_1step d5 (
    .A0(d4_a0out), .A1(d4_a1out), .E(d4_eout), .A0out(d5_a0out), .A1out(d5_a1out), .Eout(d5_eout));
  double_dabble_1step d2 (
    .A0(d1_a0out), .A1(d1_a1out), .E(d1_eout), .A0out(d2_a0out), .A1out(d2_a1out), .Eout(d2_eout));
  double_dabble_1step d6 (
    .A0(d5_a0out), .A1(d5_a1out), .E(d5_eout), .A0out(d6_a0out), .A1out(d6_a1out), .Eout(d6_eout));
  double_dabble_1step d3 (
    .A0(d2_a0out), .A1(d2_a1out), .E(d2_eout), .A0out(d3_a0out), .A1out(d3_a1out), .Eout(d3_eout));
  double_dabble_1step d7 (.A0(d6_a0out), .A1(d6_a1out), .E(d6_eout), .A0out(A0), .A1out(A1));  // open: Eout
  double_dabble_1step d4 (
    .A0(d3_a0out), .A1(d3_a1out), .E(d3_eout), .A0out(d4_a0out), .A1out(d4_a1out), .Eout(d4_eout));
endmodule

module print_number (
  input  [6:0] E,
  input  [1:0] P,
  output [7:0] S0,
  output [7:0] S1
);

  double_dabble dd1 (.E(E), .A0(S0[3:0]), .A1(S1[3:0]));

  assign S0[7:4] = {2'b00, P[0], 1'b0};
  assign S1[7:4] = {2'b00, P[1], 1'b0};
endmodule

module print_hour (
  input  [6:0] cS,
  input  [5:0] S,
  input  [5:0] M,
  input  [4:0] H,
  input  Chrono,
  output [7:0] S0,
  output [7:0] S1,
  output [7:0] S2,
  output [7:0] S3,
  output [7:0] S4,
  output [7:0] S5
);

  wire and_1_out, and_2_out, not_1_out, not_2_out, not_3_out, not_4_out, not_5_out, not_6_out;
  wire [7:0] p1_s0, p1_s1, p2_s0, p2_s1, p3_s0, p3_s1, pm5_s0, pm5_s1;

  not not_1 (not_1_out, H[0]);
  not not_2 (not_2_out, H[1]);
  not not_3 (not_3_out, H[2]);
  not not_4 (not_4_out, H[3]);
  not not_5 (not_5_out, H[4]);
  and and_1 (and_1_out, not_1_out, not_2_out, not_3_out, not_4_out, not_5_out);
  and and_2 (and_2_out, and_1_out, Chrono);
  not not_6 (not_6_out, and_2_out);
  print_number pm5 (.E(cS), .P(2'b00), .S0(pm5_s0), .S1(pm5_s1));
  print_number p1 (.E({1'b0, S}), .P({1'b0, Chrono}), .S0(p1_s0), .S1(p1_s1));
  print_number p2 (.E({1'b0, M}), .P(2'b01), .S0(p2_s0), .S1(p2_s1));
  print_number p3 (.E({2'b00, H}), .P(2'b01), .S0(p3_s0), .S1(p3_s1));
  Multiplexer #(.width(8)) multiplexer_1 (.in0(pm5_s0), .in1(p1_s0), .out(S0), .sel(not_6_out));
  Multiplexer #(.width(8)) multiplexer_2 (.in0(pm5_s1), .in1(p1_s1), .out(S1), .sel(not_6_out));
  Multiplexer #(.width(8)) multiplexer_3 (.in0(p1_s0), .in1(p2_s0), .out(S2), .sel(not_6_out));
  Multiplexer #(.width(8)) multiplexer_4 (.in0(p1_s1), .in1(p2_s1), .out(S3), .sel(not_6_out));
  Multiplexer #(.width(8)) multiplexer_5 (.in0(p1_s1), .in1(p3_s0), .out(S4), .sel(not_6_out));
  Multiplexer #(.width(8)) multiplexer_6 (.in0(p2_s1), .in1(p3_s1), .out(S5), .sel(not_6_out));
endmodule

module chrono (
  input  [2:0] Menu,
  input  Enter,
  output [47:0] Hour
);

  wire and_1_out, and_2_out, and_3_out, clock_1_out, not_1_out, not_2_out, not_3_out;
  wire [1:0] counter_1_q;
  wire [4:0] t_h;
  wire [5:0] t_m, t_s;
  wire [6:0] t_cs;

  not not_1 (not_1_out, Menu[0]);
  not not_2 (not_2_out, Menu[1]);
  and and_1 (and_1_out, not_1_out, not_2_out, Menu[2]);
  and and_2 (and_2_out, and_1_out, Enter);
  Counter #(.max('h2), .width(2)) counter_1 (
    .clr(1'b0), .load(1'b0), .up(not_3_out), .count(and_2_out), .clk(clock_1_out), .Q(counter_1_q));  // open: D, carry
  not not_3 (not_3_out, 1'b0);
  Clock #(.highDuration(125000), .lowDuration(125000)) clock_1 (.out(clock_1_out));
  and and_3 (and_3_out, ~counter_1_q[0], ~counter_1_q[1]);  // AND_Gate
  timer t (.Enable(counter_1_q[0]), .R(and_3_out), .cS(t_cs), .S(t_s), .M(t_m), .H(t_h));
  print_hour ph (
    .cS(t_cs), .S(t_s), .M(t_m), .H(t_h), .Chrono(1'b1), .S0(Hour[7:0]), .S1(Hour[15:8]), .S2(Hour[23:16]),
    .S3(Hour[31:24]), .S4(Hour[39:32]), .S5(Hour[47:40]));
endmodule

module modulo59 (
  input  [5:0] E,
  output [5:0] S,
  output carry
);

  and and_1 (carry, E[2], E[3], E[4], E[5]);
  Subtractor #(.width(6)) subtractor_1 (.a(E), .b({{4{carry}}, 2'b00}), .out(S));  // open: bin, bout
endmodule

module modulo24 (
  input  [4:0] H,
  output [4:0] Hout
);

  wire and_1_out;
  wire [4:0] multiplexer_1_out;

  and and_1 (and_1_out, H[3], H[4]);
  Multiplexer #(.width(5)) multiplexer_1 (.in0({5{1'b0}}), .in1(5'b11000), .out(multiplexer_1_out), .sel(and_1_out));
  Subtractor #(.width(5)) subtractor_1 (.a(H), .b(multiplexer_1_out), .out(Hout));  // open: bin, bout
endmodule

module Horloge (
  input  [2:0] Menu,
  input  Eplus,
  input  Enter,
  input  Eminus,
  output [47:0] HourTexte,
  output [10:0] Hour
);

  wire and_1_out, not_1_out, not_2_out, not_3_out;
  wire [1:0] o2_selector;
  wire [4:0] t_h;
  wire [5:0] t_m, t_s;
  wire [7:0] ph_s0, ph_s1, ph_s2, ph_s3, ph_s4, ph_s5;

  not not_1 (not_1_out, Menu[1]);
  not not_2 (not_2_out, Menu[2]);
  not not_3 (not_3_out, and_1_out);
  and and_1 (and_1_out, Menu[0], not_1_out, not_2_out);
  timer t (.Enable(not_3_out), .R(1'b0), .S(t_s), .M(t_m), .H(t_h));  // open: cS
  offset2 o2 (
    .M(t_m), .Eplus(Eplus), .Enable(and_1_out), .Eminus(Eminus), .Switch(Enter), .H(t_h), .Mout(Hour[5:0]),
    .Hout(Hour[10:6]), .Selector(o2_selector));
  print_hour ph (
    .S(t_s), .M(Hour[5:0]), .H(Hour[10:6]), .Chrono(1'b0), .S0(ph_s0), .S1(ph_s1), .S2(ph_s2), .S3(ph_s3),
    .S4(ph_s4), .S5(ph_s5));  // open: cS
  clignotant cl (
    .T1({ph_s1, ph_s0}), .T2({ph_s3, ph_s2}), .T3({ph_s5, ph_s4}), .Selector(o2_selector),
    .S1(HourTexte[15:0]), .S2(HourTexte[31:16]), .S3(HourTexte[47:32]));
endmodule

module offset2 (
  input  [5:0] M,
  input  Eplus,
  input  Enable,
  input  Eminus,
  input  Switch,
  input  [4:0] H,
  output [5:0] Mout,
  output [4:0] Hout,
  output [1:0] Selector
);

  wire adder_1_cout, adder_2_cout, and_1_out, and_2_out, and_3_out, and_4_out, and_5_out, and_6_out,
       and_7_out, and_8_out, clock_1_out, clock_2_out, m59_carry, nand_3_out, not_1_out, subtractor_1_bout,
       subtractor_3_bout, t_ff_1_q, t_ff_1_qn;
  wire [4:0] adder_1_out, adder_4_out, bm2_s, bp2_s, multiplexer_3_out, multiplexer_4_out, subtractor_3_out,
       subtractor_4_out;
  wire [5:0] adder_2_out, adder_3_out, Bminus_s, Bplus_s, multiplexer_1_out, multiplexer_2_out,
       subtractor_1_out, subtractor_2_out;

  Clock #(.highDuration(32), .lowDuration(32)) clock_1 (.out(clock_1_out));
  and and_1 (and_1_out, Eplus, Enable);
  and and_2 (and_2_out, Enable, Eminus);
  T_Flip_Flop t_ff_1 (.T(Switch), .clk(clock_1_out), .Q(t_ff_1_q), .Qn(t_ff_1_qn));  // open: reset, preset
  not not_1 (not_1_out, t_ff_1_qn);
  Clock #(.highDuration(4), .lowDuration(4)) clock_2 (.out(clock_2_out));
  nand nand_1 (Selector[0], t_ff_1_qn, Enable);
  nand nand_2 (Selector[1], Enable, not_1_out);
  and and_3 (and_3_out, and_1_out, t_ff_1_q);
  and and_4 (and_4_out, and_2_out, t_ff_1_q);
  and and_5 (and_5_out, and_1_out, t_ff_1_qn);
  and and_6 (and_6_out, and_2_out, t_ff_1_qn);
  base60Increment Bplus (.RESET(1'b0), .Enable(and_3_out), .Clk(clock_2_out), .S(Bplus_s));  // open: Overflow
  base60Increment Bminus (.RESET(1'b0), .Enable(and_4_out), .Clk(clock_2_out), .S(Bminus_s));  // open: Overflow
  base24Increment bp2 (.RESET(1'b0), .Enable(and_5_out), .Clk(clock_2_out), .S(bp2_s));  // open: Overflow
  base24Increment bm2 (.RESET(1'b0), .Enable(and_6_out), .Clk(clock_2_out), .S(bm2_s));  // open: Overflow
  Subtractor #(.width(6)) subtractor_1 (
    .a(Bplus_s), .b(Bminus_s), .out(subtractor_1_out), .bout(subtractor_1_bout));  // open: bin
  Multiplexer #(.width(6)) multiplexer_1 (
    .in0({6{1'b0}}), .in1(6'b000100), .out(multiplexer_1_out), .sel(subtractor_1_bout));
  Subtractor #(.width(6)) subtractor_2 (
    .a(subtractor_1_out), .b(multiplexer_1_out), .out(subtractor_2_out));  // open: bin, bout
  Adder #(.width(5)) adder_1 (.a(H), .b(bp2_s), .out(adder_1_out), .cin(m59_carry), .cout(adder_1_cout));
  nand nand_3 (nand_3_out, adder_1_cout, subtractor_3_bout);
  and and_7 (and_7_out, adder_1_cout, nand_3_out);
  Adder #(.width(6)) adder_2 (.a(M), .b(subtractor_2_out), .out(adder_2_out), .cout(adder_2_cout));  // open: cin
  Multiplexer #(.width(6)) multiplexer_2 (
    .in0({6{1'b0}}), .in1(6'b000100), .out(multiplexer_2_out), .sel(adder_2_cout));
  Subtractor #(.width(5)) subtractor_3 (
    .a(adder_1_out), .b(bm2_s), .out(subtractor_3_out), .bout(subtractor_3_bout));  // open: bin
  and and_8 (and_8_out, nand_3_out, subtractor_3_bout);
  Adder #(.width(6)) adder_3 (.a(adder_2_out), .b(multiplexer_2_out), .out(adder_3_out));  // open: cin, cout
  Subtractor #(.width(5)) subtractor_4 (
    .a(subtractor_3_out), .b(multiplexer_3_out), .out(subtractor_4_out));  // open: bin, bout
  Multiplexer #(.width(5)) multiplexer_3 (.in0({5{1'b0}}), .in1(5'b01000), .out(multiplexer_3_out), .sel(and_8_out));
  Multiplexer #(.width(5)) multiplexer_4 (.in0({5{1'b0}}), .in1(5'b01000), .out(multiplexer_4_out), .sel(and_7_out));
  Adder #(.width(5)) adder_4 (
    .a(subtractor_4_out), .b(multiplexer_4_out), .out(adder_4_out), .cin(adder_2_cout));  // open: cout
  modulo59 m59 (.E(adder_3_out), .S(Mout), .carry(m59_carry));
  modulo24 M2 (.H(adder_4_out), .Hout(Hout));
endmodule

module antiRebond (
  input  dataIn,
  output o
);

  wire and_1_out, and_2_out, and_3_out, and_4_out, clock_1_out, d_ff_1_q, d_ff_2_q, d_ff_3_q, d_ff_4_q;

  Clock clock_1 (.out(clock_1_out));
  D_Flip_Flop d_ff_1 (.D(dataIn), .clk(clock_1_out), .Q(d_ff_1_q));  // open: Qn, preset, reset
  D_Flip_Flop d_ff_2 (.D(d_ff_1_q), .clk(clock_1_out), .Q(d_ff_2_q));  // open: Qn, preset, reset
  D_Flip_Flop d_ff_3 (.D(d_ff_2_q), .clk(clock_1_out), .Q(d_ff_3_q));  // open: Qn, preset, reset
  D_Flip_Flop d_ff_4 (.D(d_ff_3_q), .clk(clock_1_out), .Q(d_ff_4_q));  // open: Qn, preset, reset
  and and_1 (and_1_out, d_ff_3_q, d_ff_4_q);
  and and_2 (and_2_out, d_ff_2_q, d_ff_4_q);
  and and_3 (and_3_out, d_ff_1_q, d_ff_4_q);
  and and_4 (and_4_out, d_ff_1_q, d_ff_2_q, d_ff_3_q);
  or or_1 (o, and_1_out, and_2_out, and_3_out, and_4_out);
endmodule

module reader (
  input  A,
  input  B,
  output Eplus,
  output Emoins
);

  wire and_1_out, and_2_out, and_3_out, and_4_out, d_ff_1_q, d_ff_2_q, d_ff_3_q, d_ff_4_q, not_1_out,
       not_2_out, not_3_out, not_4_out;

  D_Flip_Flop d_ff_1 (.D(not_1_out), .clk(A), .Q(d_ff_1_q), .reset(and_1_out));  // open: Qn, preset
  not not_1 (not_1_out, B);
  and and_1 (and_1_out, B, A);
  D_Flip_Flop d_ff_2 (.D(not_2_out), .clk(B), .Q(d_ff_2_q), .reset(and_2_out));  // open: Qn, preset
  not not_2 (not_2_out, A);
  and and_2 (and_2_out, B, A);
  D_Flip_Flop d_ff_3 (.D(B), .clk(not_3_out), .Q(d_ff_3_q), .reset(and_3_out));  // open: Qn, preset
  not not_3 (not_3_out, A);
  and and_3 (and_3_out, ~B, ~A);  // AND_Gate
  D_Flip_Flop d_ff_4 (.D(A), .clk(not_4_out), .Q(d_ff_4_q), .reset(and_4_out));  // open: Qn, preset
  not not_4 (not_4_out, B);
  and and_4 (and_4_out, ~B, ~A);  // AND_Gate
  or or_1 (Eplus, d_ff_1_q, d_ff_3_q);
  or or_2 (Emoins, d_ff_2_q, d_ff_4_q);
endmodule

module encodeur (
  input  a,
  input  b,
  output Emoins,
  output Eplus
);

  wire ah_o, ou_o;

  antiRebond ou (.dataIn(a), .o(ou_o));
  antiRebond ah (.dataIn(b), .o(ah_o));
  reader nh (.A(ou_o), .B(ah_o), .Eplus(Eplus), .Emoins(Emoins));
endmodule

module print_menu (
  input  [2:0] Menu,
  output [47:0] Current_menu
);

  Multiplexer #(.select(3), .width(48)) multiplexer_1 (
    .in0(48'h1f1f11171c19), .in1(48'h1f1a0e1b1f11), .in2(48'ha140a191501), .in3(48'ha140a191502),
    .in4(48'hc1119171617), .in5(48'h1f1b12150e19), .in6(48'h100a150e1f01), .in7(48'h100a150e1f02),
    .out(Current_menu), .sel(Menu));

  // Notes on the sheet:
  //   Dans l'ordre : Game 2, Hour, set H, Alarm, chrono, timR, game1
endmodule

module screen_managment (
  input  Eplus,
  input  Eminus,
  input  Enter,
  input  Menu,
  output Sonnerie,
  output [7:0] S0,
  output [7:0] S1,
  output [7:0] S2,
  output [7:0] S3,
  output [7:0] S4,
  output [7:0] S5
);

  wire and_1_out, and_2_out, and_3_out, and_4_out, d_ff_1_q, d_ff_2_q, not_1_out, not_2_out, ts2_ring,
       ts_ring;
  wire [2:0] mm_menu;
  wire [10:0] h_hour;
  wire [11:0] a1_alarmout, a2_alarmout;
  wire [47:0] a1_text, a2_text, c_hour, h_hourtexte, pm_current_menu, ssm_printedtext;

  D_Flip_Flop d_ff_1 (.D(1'b0), .clk(1'b0), .Q(d_ff_1_q), .preset(Menu), .reset(and_1_out));  // open: Qn
  and and_1 (and_1_out, Enter, not_1_out);
  and and_2 (and_2_out, Menu, d_ff_1_q);
  and and_3 (and_3_out, Menu, d_ff_2_q);
  not not_1 (not_1_out, Menu);
  D_Flip_Flop d_ff_2 (.D(1'b0), .clk(1'b0), .Q(d_ff_2_q), .preset(Enter), .reset(and_4_out));  // open: Qn
  and and_4 (and_4_out, and_3_out, not_2_out);
  not not_2 (not_2_out, Enter);
  menu_managment mm (.Reset(and_3_out), .Switch(and_2_out), .Menu(mm_menu));
  alarm a2 (
    .Menu(mm_menu), .nb(1'b1), .Eplus(Eplus), .Eminus(Eminus), .Enter(Enter), .Text(a2_text),
    .AlarmOut(a2_alarmout));
  alarm a1 (
    .Menu(mm_menu), .nb(1'b0), .Eplus(Eplus), .Eminus(Eminus), .Enter(Enter), .Text(a1_text),
    .AlarmOut(a1_alarmout));
  chrono c (.Menu(mm_menu), .Enter(Enter), .Hour(c_hour));
  Horloge h (.Menu(mm_menu), .Eplus(Eplus), .Enter(Enter), .Eminus(Eminus), .HourTexte(h_hourtexte), .Hour(h_hour));
  print_menu pm (.Menu(mm_menu), .Current_menu(pm_current_menu));
  TestSonnerie ts2 (.Hour(h_hour), .Alarm(a2_alarmout), .Ring(ts2_ring));
  TestSonnerie ts (.Hour(h_hour), .Alarm(a1_alarmout), .Ring(ts_ring));
  sub_screen_managment ssm (
    .M0(h_hourtexte), .M1(h_hourtexte), .M2(a1_text), .M3(a2_text), .M4(c_hour), .Mtext(pm_current_menu),
    .MenuOn(d_ff_1_q), .MenuNb(mm_menu), .PrintedText(ssm_printedtext));  // open: M5, M6, M7
  or or_1 (Sonnerie, ts2_ring, ts_ring);
  print_text Pt (.Text(ssm_printedtext), .S0(S0), .S1(S1), .S2(S2), .S3(S3), .S4(S4), .S5(S5));

  // Notes on the sheet:
  //   Ajouter les différents menus et connecter leur texte
  //   Un caractere=1 octets
endmodule

module print_text (
  input  [47:0] Text,
  output [7:0] S0,
  output [7:0] S1,
  output [7:0] S2,
  output [7:0] S3,
  output [7:0] S4,
  output [7:0] S5
);

  decodeur_sympa d1 (.P(Text[5]), .E(Text[4:0]), .S(S0));
  decodeur_sympa d2 (.P(Text[13]), .E(Text[12:8]), .S(S1));
  decodeur_sympa d3 (.P(Text[21]), .E(Text[20:16]), .S(S2));
  decodeur_sympa d4 (.P(Text[29]), .E(Text[28:24]), .S(S3));
  decodeur_sympa d5 (.P(Text[37]), .E(Text[36:32]), .S(S4));
  decodeur_sympa d6 (.P(Text[45]), .E(Text[44:40]), .S(S5));
endmodule

module menu_managment (
  input  Reset,
  input  Switch,
  output [2:0] Menu
);

  wire and_1_out, clock_1_out, not_1_out;

  Counter #(.max('h7), .width(3)) counter_1 (
    .clr(and_1_out), .load(1'b0), .up(not_1_out), .count(Switch), .clk(clock_1_out), .Q(Menu));  // open: D, carry
  and and_1 (and_1_out, Reset, ~Switch);  // AND_Gate
  not not_1 (not_1_out, 1'b0);
  Clock #(.highDuration(32), .lowDuration(32)) clock_1 (.out(clock_1_out));
endmodule

module sub_screen_managment (
  input  [47:0] M0,
  input  [47:0] M1,
  input  [47:0] M2,
  input  [47:0] M3,
  input  [47:0] M4,
  input  [47:0] M5,
  input  [47:0] M6,
  input  [47:0] M7,
  input  [47:0] Mtext,
  input  MenuOn,
  input  [2:0] MenuNb,
  output [47:0] PrintedText
);

  wire [47:0] multiplexer_1_out;

  Multiplexer #(.select(3), .width(48)) multiplexer_1 (
    .in0(M0), .in1(M1), .in2(M2), .in3(M3), .in4(M4), .in5(M5), .in6(M6), .in7(M7), .out(multiplexer_1_out),
    .sel(MenuNb));
  Multiplexer #(.width(48)) multiplexer_2 (.in0(multiplexer_1_out), .in1(Mtext), .out(PrintedText), .sel(MenuOn));
endmodule

module base100Increment (
  input  Enable,
  input  Clk,
  input  Reset,
  output [6:0] S,
  output Clkout,
  output Overflow
);

  wire d_ff_1_q, not_1_out, or_1_out, t_ff_1_qn, t_ff_2_qn, t_ff_3_qn, t_ff_4_qn, t_ff_5_qn, t_ff_6_qn;

  T_Flip_Flop t_ff_1 (.T(Enable), .clk(Clk), .Q(S[0]), .Qn(t_ff_1_qn), .reset(or_1_out));  // open: preset
  T_Flip_Flop t_ff_2 (.T(Enable), .clk(t_ff_1_qn), .Q(S[1]), .Qn(t_ff_2_qn), .reset(or_1_out));  // open: preset
  T_Flip_Flop t_ff_3 (.T(Enable), .clk(t_ff_2_qn), .Q(S[2]), .Qn(t_ff_3_qn), .reset(or_1_out));  // open: preset
  T_Flip_Flop t_ff_4 (.T(Enable), .clk(t_ff_3_qn), .Q(S[3]), .Qn(t_ff_4_qn), .reset(or_1_out));  // open: preset
  T_Flip_Flop t_ff_5 (.T(Enable), .clk(t_ff_4_qn), .Q(S[4]), .Qn(t_ff_5_qn), .reset(or_1_out));  // open: preset
  T_Flip_Flop t_ff_6 (.T(Enable), .clk(t_ff_5_qn), .Q(S[5]), .Qn(t_ff_6_qn), .reset(or_1_out));  // open: preset
  T_Flip_Flop t_ff_7 (.T(Enable), .clk(t_ff_6_qn), .Q(S[6]), .Qn(Clkout), .reset(or_1_out));  // open: preset
  or or_1 (or_1_out, d_ff_1_q, Reset);
  and and_1 (Overflow, S[6], S[5], S[2]);
  not not_1 (not_1_out, S[0]);
  D_Flip_Flop d_ff_1 (.D(1'b1), .clk(Overflow), .Q(d_ff_1_q), .reset(not_1_out));  // open: Qn, preset
endmodule

module decodeur_sympa (
  input  P,
  input  [4:0] E,
  output [7:0] S
);

  wire and_1_out, and_2_out, and_3_out, and_4_out, and_5_out, and_6_out, and_7_out, and_8_out, and_9_out,
       and_10_out, and_11_out, and_12_out, and_13_out, and_14_out, and_15_out, and_16_out, and_17_out,
       and_18_out, and_19_out, and_20_out, and_21_out, and_22_out, and_23_out, and_24_out, and_25_out,
       and_26_out, and_27_out, and_28_out, and_29_out, and_30_out, and_31_out, and_32_out, and_33_out,
       and_34_out, and_35_out, and_36_out, and_37_out, and_38_out, and_39_out, and_40_out, and_41_out,
       and_42_out, and_43_out, and_44_out, and_45_out, and_46_out, and_47_out, and_48_out, and_49_out,
       and_50_out, and_51_out, and_52_out, and_53_out, and_54_out, and_55_out, and_56_out, and_57_out,
       and_58_out, and_59_out, and_60_out, not_1_out, not_2_out, not_3_out, not_4_out, not_5_out;

  not not_1 (not_1_out, E[4]);
  not not_2 (not_2_out, E[3]);
  not not_3 (not_3_out, E[2]);
  not not_4 (not_4_out, E[1]);
  not not_5 (not_5_out, E[0]);
  and and_1 (and_1_out, not_3_out, not_4_out, not_5_out);
  and and_2 (and_2_out, not_1_out, not_2_out, E[1]);
  and and_3 (and_3_out, not_1_out, E[1], not_5_out);
  and and_4 (and_4_out, not_2_out, E[2], not_4_out, E[0]);
  and and_5 (and_5_out, not_1_out, E[2], E[1]);
  and and_6 (and_6_out, not_1_out, E[3], not_3_out, not_4_out);
  and and_7 (and_7_out, not_1_out, E[3], not_5_out);
  and and_8 (and_8_out, E[3], not_3_out, not_5_out);
  and and_9 (and_9_out, E[4], E[2], not_4_out, E[0]);
  and and_10 (and_10_out, not_1_out, not_2_out, not_4_out, not_5_out);
  and and_11 (and_11_out, not_1_out, not_3_out, not_4_out);
  and and_12 (and_12_out, not_1_out, not_3_out, not_5_out);
  and and_13 (and_13_out, not_2_out, not_3_out, E[0]);
  and and_14 (and_14_out, not_1_out, not_2_out, E[1], E[0]);
  and and_15 (and_15_out, E[3], not_3_out, not_4_out, not_5_out);
  and and_16 (and_16_out, E[3], E[2], not_4_out, E[0]);
  and and_17 (and_17_out, E[4], not_2_out, not_4_out, E[0]);
  and and_18 (and_18_out, E[4], E[3], not_4_out, not_5_out);
  and and_19 (and_19_out, not_1_out, not_2_out, not_4_out);
  and and_20 (and_20_out, not_1_out, not_3_out, not_4_out);
  and and_21 (and_21_out, not_2_out, not_3_out, not_4_out);
  and and_22 (and_22_out, not_1_out, not_4_out, E[0]);
  and and_23 (and_23_out, not_2_out, E[0]);
  and and_24 (and_24_out, not_2_out, E[2], E[1]);
  and and_25 (and_25_out, not_1_out, E[3], not_3_out);
  and and_26 (and_26_out, E[3], not_3_out, E[1], not_5_out);
  and and_27 (and_27_out, E[4], E[3], E[2], not_4_out, not_5_out);
  and and_28 (and_28_out, not_2_out, not_3_out, not_4_out, not_5_out);
  and and_29 (and_29_out, not_1_out, not_2_out, E[1], not_5_out);
  and and_30 (and_30_out, not_2_out, not_3_out, E[1], E[0]);
  and and_31 (and_31_out, not_1_out, E[2], not_4_out, E[0]);
  and and_32 (and_32_out, not_1_out, E[3], not_4_out);
  and and_33 (and_33_out, not_1_out, E[3], not_3_out, E[0]);
  and and_34 (and_34_out, E[3], E[2], not_4_out);
  and and_35 (and_35_out, E[3], E[2], not_5_out);
  and and_36 (and_36_out, E[4], not_2_out, not_4_out, not_5_out);
  and and_37 (and_37_out, E[4], not_2_out, E[1], E[0]);
  and and_38 (and_38_out, E[4], E[3], E[1], not_5_out);
  and and_39 (and_39_out, not_3_out, not_4_out, not_5_out);
  and and_40 (and_40_out, not_1_out, E[1], not_5_out);
  and and_41 (and_41_out, E[3], not_3_out, E[1], E[0]);
  and and_42 (and_42_out, not_1_out, E[3], E[2]);
  and and_43 (and_43_out, E[4], not_2_out);
  and and_44 (and_44_out, E[4], not_4_out);
  and and_45 (and_45_out, not_4_out, not_5_out);
  and and_46 (and_46_out, not_1_out, E[2], not_5_out);
  and and_47 (and_47_out, not_2_out, E[2], not_4_out);
  and and_48 (and_48_out, not_1_out, E[3], not_3_out);
  and and_49 (and_49_out, not_1_out, E[3], E[1]);
  and and_50 (and_50_out, E[3], not_3_out, E[1]);
  and and_51 (and_51_out, E[4], not_2_out, not_4_out);
  and and_52 (and_52_out, E[4], not_3_out, not_5_out);
  and and_53 (and_53_out, not_1_out, not_3_out, E[1]);
  and and_54 (and_54_out, not_1_out, not_2_out, E[2], not_4_out);
  and and_55 (and_55_out, E[2], E[1], not_5_out);
  and and_56 (and_56_out, E[3], not_3_out);
  and and_57 (and_57_out, E[3], not_4_out, E[0]);
  and and_58 (and_58_out, not_1_out, E[3], E[1]);
  and and_59 (and_59_out, E[4], not_3_out, not_4_out, E[0]);
  and and_60 (and_60_out, E[4], not_2_out, E[2], E[1]);
  or or_1 (S[0], and_1_out, and_2_out, and_3_out, and_4_out, and_5_out, and_6_out, and_7_out, and_8_out, and_9_out);
  or or_2 (S[1], and_10_out, and_11_out, and_12_out, and_13_out, and_14_out, and_15_out, and_16_out, and_17_out, and_18_out);
  or or_3 (S[2], and_19_out, and_20_out, and_21_out, and_22_out, and_23_out, and_24_out, and_25_out, and_26_out, and_27_out);
  or or_4 (S[4], and_39_out, and_40_out, and_41_out, and_42_out, and_43_out, and_44_out);
  or or_5 (S[5], and_45_out, and_46_out, and_47_out, and_48_out, and_49_out, and_50_out, and_51_out, and_52_out);
  or or_6 (S[6], and_53_out, and_54_out, and_55_out, and_56_out, and_57_out, and_58_out, and_59_out, and_60_out);
  or or_7 (S[3], and_28_out, and_29_out, and_30_out, and_31_out, and_32_out, and_33_out, and_34_out, and_35_out, and_36_out, and_37_out, and_38_out);

  assign S[7] = P;
endmodule

module alarm (
  input  [2:0] Menu,
  input  nb,
  input  Eplus,
  input  Eminus,
  input  Enter,
  output [47:0] Text,
  output [11:0] AlarmOut
);

  wire and_1_out, and_2_out, and_3_out, and_4_out, and_5_out, clock_1_out, multiplexer_1_out, not_1_out,
       not_2_out, not_3_out, not_4_out, not_5_out, t_ff_1_q, t_ff_1_qn, t_ff_2_q, t_ff_3_q;
  wire [1:0] counter_1_q;

  and and_1 (and_1_out, Menu[0], Menu[1], not_1_out);
  not not_1 (not_1_out, Menu[2]);
  not not_2 (not_2_out, Menu[0]);
  and and_2 (and_2_out, not_2_out, Menu[1], not_3_out);
  not not_3 (not_3_out, Menu[2]);
  Counter #(.max('h2), .width(2)) counter_1 (
    .clr(not_4_out), .load(not_4_out), .up(1'b1), .count(Enter), .clk(clock_1_out), .Q(counter_1_q));  // open: D, carry
  not not_4 (not_4_out, 1'b1);
  Clock #(.highDuration(50000), .lowDuration(50000)) clock_1 (.out(clock_1_out));
  Multiplexer multiplexer_1 (.in0(and_2_out), .in1(and_1_out), .out(multiplexer_1_out), .sel(nb));
  and and_3 (and_3_out, multiplexer_1_out, t_ff_1_q);
  not not_5 (not_5_out, counter_1_q[1]);
  T_Flip_Flop t_ff_1 (.T(1'b1), .clk(and_4_out), .Q(t_ff_1_q), .Qn(t_ff_1_qn));  // open: reset, preset
  and and_4 (and_4_out, counter_1_q[1], Enter);
  and and_5 (and_5_out, Enter, not_5_out);
  offset2 o2 (
    .M({6{1'b0}}), .Eplus(Eplus), .Enable(and_3_out), .Eminus(and_5_out), .Switch(Eminus), .H({5{1'b0}}),
    .Mout(AlarmOut[5:0]), .Hout(AlarmOut[10:6]));  // open: Selector
  T_Flip_Flop t_ff_2 (.T(t_ff_1_qn), .clk(Eplus), .Q(t_ff_2_q));  // open: Qn, reset, preset
  T_Flip_Flop t_ff_3 (.T(t_ff_1_qn), .clk(Eminus), .Q(t_ff_3_q));  // open: Qn, reset, preset
  xor xor_1 (AlarmOut[11], t_ff_2_q, t_ff_3_q);
  print_number pn1 (.E({1'b0, AlarmOut[5:0]}), .P(2'b00), .S0(Text[7:0]), .S1(Text[15:8]));
  print_number pn2 (.E({2'b00, AlarmOut[10:6]}), .P(2'b01), .S0(Text[23:16]), .S1(Text[31:24]));
  Multiplexer #(.width(16)) multiplexer_2 (.in0(16'h170f), .in1(16'h1716), .out(Text[47:32]), .sel(AlarmOut[11]));
endmodule

module base3Incremenrt (
  input  Enable,
  input  Clk,
  output S1,
  output S2
);

  wire and_1_out, and_2_out, not_1_out, not_2_out, t_ff_1_qn, t_ff_3_q;

  T_Flip_Flop t_ff_1 (.T(Enable), .clk(Clk), .Q(S1), .Qn(t_ff_1_qn), .reset(t_ff_3_q));  // open: preset
  T_Flip_Flop t_ff_2 (.T(Enable), .clk(t_ff_1_qn), .Q(S2), .reset(t_ff_3_q));  // open: Qn, preset
  not not_1 (not_1_out, S1);
  not not_2 (not_2_out, S2);
  and and_1 (and_1_out, S2, S1);
  T_Flip_Flop t_ff_3 (.T(1'b1), .clk(and_1_out), .Q(t_ff_3_q), .reset(and_2_out));  // open: Qn, preset
  and and_2 (and_2_out, not_2_out, not_1_out);
endmodule

module TestSonnerie (
  input  [10:0] Hour,
  input  [11:0] Alarm,
  output Ring
);

  wire [10:0] not_1_out, xor_1_out;

  assign xor_1_out = Hour ^ Alarm[10:0];  // XOR_Gate xor_1, 11 bits wide
  assign not_1_out = ~xor_1_out;  // NOT_Gate not_1, 11 bits wide
  and and_1 (Ring, not_1_out[0], not_1_out[1], not_1_out[2], not_1_out[3], not_1_out[4], not_1_out[5], not_1_out[7], not_1_out[8], not_1_out[9], not_1_out[10], not_1_out[6], Alarm[11]);
endmodule

module simuDeMain (
  input  in_1,
  input  in_2,
  input  in_3,
  input  in_4,
  output out_5
);

  wire not_1_out;
  wire [7:0] main_1_s0, main_1_s1, main_1_s2, main_1_s3, main_1_s4, main_1_s5;

  main main_1 (
    .em(in_4), .ep(in_3), .Encoder_button(not_1_out), .Menu(in_1), .led(out_5), .S0(main_1_s0),
    .S1(main_1_s1), .S2(main_1_s2), .S3(main_1_s3), .S4(main_1_s4), .S5(main_1_s5));  // open: a, b, vcc, gnd
  not not_1 (not_1_out, in_2);
  _7_Segment_Display u_7_segment_display_1 (
    .g(main_1_s5[6]), .f(main_1_s5[5]), .a(main_1_s5[0]), .b(main_1_s5[1]), .e(main_1_s5[4]),
    .d(main_1_s5[3]), .c(main_1_s5[2]), .dp(main_1_s5[7]));
  _7_Segment_Display u_7_segment_display_2 (
    .g(main_1_s4[6]), .f(main_1_s4[5]), .a(main_1_s4[0]), .b(main_1_s4[1]), .e(main_1_s4[4]),
    .d(main_1_s4[3]), .c(main_1_s4[2]), .dp(main_1_s4[7]));
  _7_Segment_Display u_7_segment_display_3 (
    .g(main_1_s3[6]), .f(main_1_s3[5]), .a(main_1_s3[0]), .b(main_1_s3[1]), .e(main_1_s3[4]),
    .d(main_1_s3[3]), .c(main_1_s3[2]), .dp(main_1_s3[7]));
  _7_Segment_Display u_7_segment_display_4 (
    .g(main_1_s2[6]), .f(main_1_s2[5]), .a(main_1_s2[0]), .b(main_1_s2[1]), .e(main_1_s2[4]),
    .d(main_1_s2[3]), .c(main_1_s2[2]), .dp(main_1_s2[7]));
  _7_Segment_Display u_7_segment_display_5 (
    .g(main_1_s1[6]), .f(main_1_s1[5]), .a(main_1_s1[0]), .b(main_1_s1[1]), .e(main_1_s1[4]),
    .d(main_1_s1[3]), .c(main_1_s1[2]), .dp(main_1_s1[7]));
  _7_Segment_Display u_7_segment_display_6 (
    .g(main_1_s0[6]), .f(main_1_s0[5]), .a(main_1_s0[0]), .b(main_1_s0[1]), .e(main_1_s0[4]),
    .d(main_1_s0[3]), .c(main_1_s0[2]), .dp(main_1_s0[7]));
endmodule

module clignotant (
  input  [15:0] T1,
  input  [15:0] T2,
  input  [15:0] T3,
  input  [1:0] Selector,
  output [15:0] S1,
  output [15:0] S2,
  output [15:0] S3
);

  wire clock_1_out, counter_1_carry, demultiplexer_1_out0, demultiplexer_1_out1, demultiplexer_1_out2,
       not_1_out, not_2_out;
  wire [15:0] multiplexer_1_out, multiplexer_2_out;

  Multiplexer #(.select(2), .width(16)) multiplexer_1 (
    .in0(T1), .in1(T2), .in2(T3), .in3({16{1'b0}}), .out(multiplexer_1_out), .sel(Selector));
  Clock #(.highDuration(25), .lowDuration(25)) clock_1 (.out(clock_1_out));
  Demultiplexer #(.select(2)) demultiplexer_1 (
    .out0(demultiplexer_1_out0), .out1(demultiplexer_1_out1), .out2(demultiplexer_1_out2),
    .out3(demultiplexer_1_out2), .in(1'b1), .sel(Selector));
  Counter #(.max('h4), .width(3)) counter_1 (
    .clr(not_1_out), .load(not_1_out), .up(1'b1), .count(1'b1), .clk(clock_1_out), .carry(counter_1_carry));  // open: D, Q
  not not_1 (not_1_out, 1'b1);
  Multiplexer #(.width(16)) multiplexer_2 (
    .in0(16'h1f1f), .in1(multiplexer_1_out), .out(multiplexer_2_out), .sel(not_2_out));
  not not_2 (not_2_out, counter_1_carry);
  Multiplexer #(.width(16)) multiplexer_3 (.in0(T1), .in1(multiplexer_2_out), .out(S1), .sel(demultiplexer_1_out0));
  Multiplexer #(.width(16)) multiplexer_4 (.in0(T2), .in1(multiplexer_2_out), .out(S2), .sel(demultiplexer_1_out1));
  Multiplexer #(.width(16)) multiplexer_5 (.in0(T3), .in1(multiplexer_2_out), .out(S3), .sel(demultiplexer_1_out2));
endmodule
