// Logisim project reveil.circ as structural Verilog: 10 circuits, main circuit main
module main (
  input  [6:0] E,
  output [6:0] S
);

  print_number ok (.E(E), .S0(S));  // open: S1
endmodule

module decodeur_7seg_mieux (
  input  P,
  input  [4:0] E,
  output POINT,
  output [6:0] S
);

  wire and_1_out, and_2_out, and_3_out, and_4_out, and_5_out, and_6_out, and_7_out, and_8_out, and_9_out,
       and_10_out, and_11_out, and_12_out, and_13_out, and_14_out, and_15_out, and_16_out, and_17_out,
       and_18_out, and_19_out, and_20_out, and_21_out, and_22_out, and_23_out, and_24_out, and_25_out,
       and_26_out, and_27_out, and_28_out, and_29_out, and_30_out, and_31_out, and_32_out, and_33_out,
       and_34_out, and_35_out, and_36_out, and_37_out, and_38_out, and_39_out, and_40_out, and_41_out,
       and_42_out, and_43_out, and_44_out, and_45_out, and_46_out, and_47_out, and_48_out, and_49_out,
       and_50_out, and_51_out, and_52_out, and_53_out, and_54_out, and_55_out, and_56_out, and_57_out,
       and_58_out, and_59_out, and_60_out, not_1_out, not_2_out, not_3_out, not_4_out, not_5_out;

  not not_1 (not_1_out, E[4]);
  not not_2 (not_2_out, E[4]);
  not not_3 (not_3_out, E[4]);
  not not_4 (not_4_out, E[4]);
  not not_5 (not_5_out, E[4]);
  and and_1 (and_1_out, not_3_out, not_4_out, not_5_out);
  and and_2 (and_2_out, not_1_out, E[4], not_5_out);
  and and_3 (and_3_out, not_2_out, E[4], E[4]);
  and and_4 (and_4_out, not_2_out, E[4], E[4]);
  and and_5 (and_5_out, not_1_out, E[4], E[4]);
  and and_6 (and_6_out, not_1_out, E[4], not_5_out);
  and and_7 (and_7_out, E[4], not_3_out, not_4_out);
  and and_8 (and_8_out, E[4], E[4], not_3_out, E[4]);
  and and_9 (and_9_out, not_1_out, not_2_out, not_3_out);
  and and_10 (and_10_out, not_1_out, not_2_out, not_4_out, not_5_out);
  and and_11 (and_11_out, not_1_out, not_3_out, not_4_out);
  and and_12 (and_12_out, not_2_out, E[4], E[4]);
  and and_13 (and_13_out, E[4], not_3_out, not_5_out);
  and and_14 (and_14_out, not_1_out, E[4], not_4_out, E[4]);
  and and_15 (and_15_out, E[4], not_2_out, E[4]);
  and and_16 (and_16_out, E[4], E[4], not_3_out, E[4]);
  and and_17 (and_17_out, E[4], E[4], E[4], not_5_out);
  and and_18 (and_18_out, not_1_out, not_2_out, not_4_out);
  and and_19 (and_19_out, not_1_out, not_3_out, not_4_out);
  and and_20 (and_20_out, not_2_out, not_3_out, not_4_out);
  and and_21 (and_21_out, not_1_out, not_4_out, E[4]);
  and and_22 (and_22_out, not_2_out, E[4]);
  and and_23 (and_23_out, not_3_out, not_4_out, E[4]);
  and and_24 (and_24_out, not_2_out, E[4], E[4]);
  and and_25 (and_25_out, not_1_out, E[4], not_3_out);
  and and_26 (and_26_out, E[4], not_3_out, E[4], not_5_out);
  and and_27 (and_27_out, E[4], E[4], E[4], E[4]);
  and and_28 (and_28_out, not_2_out, not_3_out, not_4_out, not_5_out);
  and and_29 (and_29_out, not_1_out, not_2_out, E[4], not_5_out);
  and and_30 (and_30_out, not_3_out, E[4], E[4]);
  and and_31 (and_31_out, not_1_out, E[4], not_4_out, E[4]);
  and and_32 (and_32_out, not_1_out, E[4], not_4_out);
  and and_33 (and_33_out, E[4], not_4_out, E[4]);
  and and_34 (and_34_out, not_1_out, E[4], E[4], not_5_out);
  and and_35 (and_35_out, E[4], not_2_out, not_4_out, not_5_out);
  and and_36 (and_36_out, E[4], E[4], E[4]);
  and and_37 (and_37_out, E[4], E[4], not_3_out, E[4]);
  and and_38 (and_38_out, not_3_out, not_5_out);
  and and_39 (and_39_out, not_2_out, E[4], not_5_out);
  and and_40 (and_40_out, E[4], E[4], E[4]);
  and and_41 (and_41_out, not_1_out, E[4], E[4]);
  and and_42 (and_42_out, E[4], not_2_out);
  and and_43 (and_43_out, not_3_out, not_4_out, not_5_out);
  and and_44 (and_44_out, not_1_out, E[4], not_5_out);
  and and_45 (and_45_out, not_2_out, E[4], not_4_out);
  and and_46 (and_46_out, not_1_out, E[4], not_3_out);
  and and_47 (and_47_out, not_1_out, E[4], E[4]);
  and and_48 (and_48_out, E[4], E[4], not_5_out);
  and and_49 (and_49_out, E[4], not_3_out, not_4_out);
  and and_50 (and_50_out, E[4], not_3_out, not_5_out);
  and and_51 (and_51_out, E[4], not_2_out, E[4], E[4]);
  and and_52 (and_52_out, not_1_out, not_3_out, E[4]);
  and and_53 (and_53_out, not_1_out, not_2_out, E[4], not_4_out);
  and and_54 (and_54_out, not_2_out, E[4], E[4], not_5_out);
  and and_55 (and_55_out, not_1_out, E[4], not_3_out);
  and and_56 (and_56_out, E[4], not_3_out, E[4]);
  and and_57 (and_57_out, E[4], not_4_out, E[4]);
  and and_58 (and_58_out, not_1_out, E[4], E[4]);
  and and_59 (and_59_out, E[4], not_3_out, not_4_out);
  and and_60 (and_60_out, E[4], E[4], not_4_out);
  or or_1 (S[0], and_1_out, and_2_out, and_3_out, and_4_out, and_5_out, and_6_out, and_7_out, and_8_out);
  or or_2 (S[1], and_9_out, and_10_out, and_11_out, and_12_out, and_13_out, and_14_out, and_15_out, and_16_out, and_17_out);
  or or_3 (S[4], and_38_out, and_39_out, and_40_out, and_41_out, and_42_out);
  or or_4 (S[5], and_43_out, and_44_out, and_45_out, and_46_out, and_47_out, and_48_out, and_49_out, and_50_out, and_51_out);
  or or_5 (S[6], and_52_out, and_53_out, and_54_out, and_55_out, and_56_out, and_57_out, and_58_out, and_59_out, and_60_out);
  or or_6 (S[2], and_18_out, and_19_out, and_20_out, and_21_out, and_22_out, and_23_out, and_24_out, and_25_out, and_26_out, and_27_out);
  or or_7 (S[3], and_28_out, and_29_out, and_30_out, and_31_out, and_32_out, and_33_out, and_34_out, and_35_out, and_36_out, and_37_out);

  assign E[3:0] = {4{E[4]}};
  assign POINT = P;

  // Notes on the sheet:
  //   Chiffres de 0a9 puis lettres de AaZ
  //   Enfin, -,=,smiley(pt1),smiley(pt2)
  //   Manque k,q,r,t,v,w,x,y
endmodule

module print_hour (
);

  shifteur7 shifteur7_1 ();  // open: E, S
endmodule

module shifteur7 (
  input  [6:0] E,
  output [6:0] S
);


  assign S = {E[5:0], 1'b0};
endmodule

module double_dabble (
  input  [6:0] E,
  output [3:0] A0,
  output [3:0] A1
);

  wire [3:0] d1_a0out, d1_a1out, d2_a0out, d2_a1out, d3_a0out, d3_a1out, d4_a0out, d4_a1out, d5_a0out,
       d5_a1out, d6_a0out, d6_a1out;
  wire [6:0] d1_eout, d2_eout, d3_eout, d4_eout, d5_eout, d6_eout;

  double_dabble_1step d1 (.A0(4'b0000), .A1(4'b0000), .E(E), .A0out(d1_a0out), .A1out(d1_a1out), .Eout(d1_eout));
  double_dabble_1step d5 (
    .A0(d4_a0out), .A1(d4_a1out), .E(d4_eout), .A0out(d5_a0out), .A1out(d5_a1out), .Eout(d5_eout));
  double_dabble_1step d2 (
    .A0(d1_a0out), .A1(d1_a1out), .E(d1_eout), .A0out(d2_a0out), .A1out(d2_a1out), .Eout(d2_eout));
  double_dabble_1step d6 (
    .A0(d5_a0out), .A1(d5_a1out), .E(d5_eout), .A0out(d6_a0out), .A1out(d6_a1out), .Eout(d6_eout));
  double_dabble_1step d3 (
    .A0(d2_a0out), .A1(d2_a1out), .E(d2_eout), .A0out(d3_a0out), .A1out(d3_a1out), .Eout(d3_eout));
  double_dabble_1step d7 (.A0(d6_a0out), .A1(d6_a1out), .E(d6_eout), .A0out(A0), .A1out(A1));  // open: Eout
  double_dabble_1step d4 (
    .A0(d3_a0out), .A1(d3_a1out), .E(d3_eout), .A0out(d4_a0out), .A1out(d4_a1out), .Eout(d4_eout));
endmodule

module comparator5 (
  input  [3:0] E,
  output [3:0] S
);

  wire and_1_out, and_2_out;

  and and_1 (and_1_out, E[0], E[2]);
  and and_2 (and_2_out, E[1], E[2]);
  or or_1 (S[3], and_1_out, and_2_out, E[3]);

  assign S[2:0] = {3{S[3]}};
endmodule

module double_dabble_1step (
  input  [3:0] A0,
  input  [3:0] A1,
  input  [6:0] E,
  output [3:0] A0out,
  output [3:0] A1out,
  output [6:0] Eout
);

  wire [0:0] adder_3_cout, adder_3_out;
  wire [2:0] adder_3_out_2;
  wire [3:0] adder_1_out, adder_5_out, and_1_out, and_2_out, c1_s, c2_s, s1_s, s2_s;

  Adder #(.width(4)) adder_1 (.a({3'b000, adder_3_cout[0]}), .b(A1), .out(adder_1_out), .cin(1'b0));  // open: cout
  comparator5 c1 (.E(A0), .S(c1_s));
  shifteur4 s1 (.E(adder_5_out), .S(s1_s));
  shifteur4 s2 (.E({adder_3_out[0], adder_3_out_2}), .S(s2_s));
  assign and_1_out = c1_s & 4'b0011;  // AND_Gate and_1, 4 bits wide
  comparator5 c2 (.E(adder_1_out), .S(c2_s));
  Adder #(.width(4)) adder_2 (.a(s2_s), .b({3'b000, E[6]}), .out(A0out), .cin(1'b0));  // open: cout
  shifteur7 s3 (.E(E), .S(Eout));
  Adder #(.width(4)) adder_3 (
    .a(A0), .b(and_1_out), .out({adder_3_out[0], adder_3_out_2}), .cin(1'b0), .cout(adder_3_cout[0]));
  assign and_2_out = 4'b0011 & c2_s;  // AND_Gate and_2, 4 bits wide
  Adder #(.width(4)) adder_4 (.a(s1_s), .b({3'b000, adder_3_out[0]}), .out(A1out), .cin(1'b0));  // open: cout
  Adder #(.width(4)) adder_5 (.a(and_2_out), .b(A1), .out(adder_5_out), .cin(1'b0));  // open: cout

  // Notes on the sheet:
  //   A0'
  //   A1'
  //   A0out
  //   A1out
endmodule

module shifteur4 (
  input  [3:0] E,
  output [3:0] S
);


  assign S = {E[2:0], 1'b0};
endmodule

module print_number (
  input  [6:0] E,
  output [6:0] S0,
  output [6:0] S1
);

  wire [3:0] dd1_a0, dd1_a1;

  double_dabble dd1 (.E(E), .A0(dd1_a0), .A1(dd1_a1));
  decodeur_Johan dj1 (.E({1'b0, dd1_a0}), .S(S0));
  decodeur_Johan dj2 (.E({1'b0, dd1_a1}), .S(S1));
endmodule

module decodeur_Johan (
  input  [4:0] E,
  output [6:0] S
);

  wire and_1_out, and_2_out, and_3_out, and_4_out, and_5_out, and_6_out, and_7_out, and_8_out, and_9_out,
       and_10_out, and_11_out, and_12_out, and_13_out, and_14_out, and_15_out, and_16_out, and_17_out,
       and_18_out, and_19_out, and_20_out, and_21_out, and_22_out, and_23_out, and_24_out, and_25_out,
       and_26_out, and_27_out, and_28_out, and_29_out, and_30_out, and_31_out, and_32_out, and_33_out,
       and_34_out, and_35_out, and_36_out, not_1_out, not_2_out, not_3_out, not_4_out;

  not not_1 (not_1_out, E[3]);
  not not_2 (not_2_out, E[2]);
  not not_3 (not_3_out, E[1]);
  not not_4 (not_4_out, E[0]);
  and and_1 (and_1_out, not_2_out, not_4_out);
  and and_2 (and_2_out, not_1_out, E[1]);
  and and_3 (and_3_out, not_1_out, E[2], E[0]);
  and and_4 (and_4_out, E[2], E[1]);
  and and_5 (and_5_out, E[3], not_2_out, not_3_out);
  and and_6 (and_6_out, E[3], not_4_out);
  and and_7 (and_7_out, not_1_out, not_2_out);
  and and_8 (and_8_out, not_1_out, not_3_out, not_4_out);
  and and_9 (and_9_out, not_2_out, not_4_out);
  and and_10 (and_10_out, not_1_out, E[1], E[0]);
  and and_11 (and_11_out, E[3], not_3_out, E[0]);
  and and_12 (and_12_out, not_1_out, not_3_out);
  and and_13 (and_13_out, not_1_out, E[0]);
  and and_14 (and_14_out, not_3_out, E[0]);
  and and_15 (and_15_out, not_1_out, E[2]);
  and and_16 (and_16_out, E[3], not_2_out);
  and and_17 (and_17_out, not_1_out, not_2_out, not_4_out);
  and and_18 (and_18_out, not_1_out, E[1], not_4_out);
  and and_19 (and_19_out, not_2_out, E[1], E[0]);
  and and_20 (and_20_out, E[2], not_3_out, E[0]);
  and and_21 (and_21_out, E[2], E[1], not_4_out);
  and and_22 (and_22_out, E[3], not_3_out);
  and and_23 (and_23_out, not_2_out, not_4_out);
  and and_24 (and_24_out, E[1], not_4_out);
  and and_25 (and_25_out, E[3], E[1]);
  and and_26 (and_26_out, E[3], E[2]);
  and and_27 (and_27_out, not_3_out, not_4_out);
  and and_28 (and_28_out, not_1_out, E[2], not_3_out);
  and and_29 (and_29_out, E[2], not_4_out);
  and and_30 (and_30_out, E[3], not_2_out);
  and and_31 (and_31_out, E[3], E[1]);
  and and_32 (and_32_out, not_2_out, E[1]);
  and and_33 (and_33_out, E[1], not_4_out);
  and and_34 (and_34_out, not_1_out, E[2], not_3_out);
  and and_35 (and_35_out, E[3], not_2_out);
  and and_36 (and_36_out, E[3], E[0]);
  or or_1 (S[0], and_1_out, and_2_out, and_3_out, and_4_out, and_5_out, and_6_out);
  or or_2 (S[1], and_7_out, and_8_out, and_9_out, and_10_out, and_11_out);
  or or_3 (S[2], and_12_out, and_13_out, and_14_out, and_15_out, and_16_out);
  or or_4 (S[3], and_17_out, and_18_out, and_19_out, and_20_out, and_21_out, and_22_out);
  or or_5 (S[4], and_23_out, and_24_out, and_25_out, and_26_out);
  or or_6 (S[5], and_27_out, and_28_out, and_29_out, and_30_out, and_31_out);
  or or_7 (S[6], and_32_out, and_33_out, and_34_out, and_35_out, and_36_out);
endmodule
